// Logisim project jrmips.circ as structural Verilog: 5 circuits, main circuit main
module main (
);

  wire and_1_out, and_4_out, and_5_out, and_6_out, and_7_out, and_8_out, and_9_out, and_10_out, and_11_out,
       and_12_out, and_13_out, Branch_output, CLOCK, Format, Halt_out, j_out, jal_out, jr_out, not_1_out,
       not_2_out, not_3_out, not_4_out, not_5_out, not_6_out, not_7_out, not_8_out, not_9_out, not_10_out,
       not_11_out, not_12_out, not_13_out, not_14_out, not_15_out, not_16_out, not_17_out, not_18_out,
       not_19_out, not_20_out, not_21_out, not_22_out, not_23_out, not_24_out, not_25_out, not_26_out,
       not_27_out, not_28_out, not_29_out, not_30_out, not_31_out, not_32_out, not_33_out, subOP, Write_out;
  wire [0:0] or_3_out;
  wire [1:0] and_2_out, multiplexer_6_out, or_2_out;
  wire [2:0] RS_t;
  wire [3:0] multiplexer_5_out, OPCODE;
  wire [7:0] adder_1_out, bitselector_1_out, Immediate, multiplexer_1_out, multiplexer_2_out,
       multiplexer_3_out, multiplexer_4_out, register_1_q;
  wire [15:0] alu_1_result, bit_extender_1_out, bit_extender_2_out, bit_extender_3_out, multiplexer_7_out,
       multiplexer_8_out, multiplexer_9_out, multiplexer_10_out, ram_1_data, register_2_q, rs, rt,
       shifter_1_out, shifter_2_out;

  DotMatrix #(.matrixcols(1), .matrixrows(1), .dotshape("circle")) dotmatrix_1 (.col0(Halt_out));
  Register register_1 (.D(multiplexer_1_out), .en(Halt_out), .Q(register_1_q), .clk(CLOCK));  // open: clr
  Clock u_Clock (.out(CLOCK));
  Multiplexer #(.width(8), .enable("false")) multiplexer_1 (
    .in0(multiplexer_2_out), .in1(Immediate), .out(multiplexer_1_out), .sel(jal_out));
  and jal (jal_out, OPCODE[0], not_2_out, not_1_out, OPCODE[3], subOP);
  not not_1 (not_1_out, OPCODE[2]);
  not not_2 (not_2_out, OPCODE[1]);
  or Halt (Halt_out, not_3_out, not_4_out, not_5_out, not_6_out);
  not not_3 (not_3_out, OPCODE[0]);
  not not_4 (not_4_out, OPCODE[1]);
  not not_5 (not_5_out, OPCODE[2]);
  not not_6 (not_6_out, OPCODE[3]);
  Adder adder_1 (.a(8'h1), .b(register_1_q), .out(adder_1_out));  // open: cin, cout
  Multiplexer #(.width(8), .enable("false")) multiplexer_2 (
    .in0(multiplexer_3_out), .in1(Immediate), .out(multiplexer_2_out), .sel(j_out));
  and j (j_out, OPCODE[0], OPCODE[1], not_7_out, OPCODE[3], subOP);
  not not_7 (not_7_out, OPCODE[2]);
  ROM #(.dataWidth(16)) rom_1 (
    .addr(register_1_q),
    .data({OPCODE, RS_t, Immediate[0], Immediate[1], Immediate[2], Immediate[3], Immediate[4], Immediate[5], Immediate[6], Immediate[7], subOP}));  // open: sel
  not not_8 (not_8_out, OPCODE[2]);
  not not_9 (not_9_out, OPCODE[3]);
  Multiplexer #(.width(8), .enable("false")) multiplexer_3 (
    .in0(multiplexer_4_out), .in1(bitselector_1_out), .out(multiplexer_3_out), .sel(jr_out));
  and jr (jr_out, OPCODE[0], not_11_out, not_10_out, OPCODE[3], not_12_out);
  not not_10 (not_10_out, OPCODE[2]);
  not not_11 (not_11_out, OPCODE[1]);
  and and_1 (and_1_out, OPCODE[0], OPCODE[1], not_8_out, not_9_out);
  BitSelector #(.width(16), .group(8)) bitselector_1 (.in(rs), .out(bitselector_1_out), .sel(1'b0));
  not not_12 (not_12_out, subOP);
  Hex_Digit_Display hex_digit_display_1 (.value(register_2_q[15:12]));  // open: dp
  Register #(.width(16)) register_2 (.D(rs), .en(and_1_out), .Q(register_2_q), .clk(CLOCK));  // open: clr
  Decoder Decoder (.Operation({subOP, OPCODE}), .Select(Format));
  Hex_Digit_Display hex_digit_display_2 (.value(register_2_q[11:8]));  // open: dp
  Hex_Digit_Display hex_digit_display_3 (.value(register_2_q[7:4]));  // open: dp
  Multiplexer #(.width(8), .enable("false")) multiplexer_4 (
    .in0(adder_1_out), .in1(Immediate), .out(multiplexer_4_out), .sel(Branch_output));
  Branch Branch (.Operation(OPCODE), .subOP(subOP), .rs(rs), .Output(Branch_output));
  Hex_Digit_Display hex_digit_display_4 (.value(register_2_q[3:0]));  // open: dp
  not not_13 (not_13_out, OPCODE[1]);
  not not_14 (not_14_out, OPCODE[3]);
  not not_15 (not_15_out, OPCODE[0]);
  not not_16 (not_16_out, OPCODE[3]);
  not not_17 (not_17_out, subOP);
  assign bit_extender_1_out = {{8{1'b0}}, adder_1_out};  // Bit_Extender bit_extender_1
  and and_2 (and_2_out[0], OPCODE[0], not_13_out, OPCODE[2], not_14_out, subOP);
  and and_3 (and_2_out[1], not_15_out, OPCODE[1], OPCODE[2], not_16_out, not_17_out);
  Multiplexer #(.width(4), .enable("false")) multiplexer_5 (
    .in0({Immediate[4], Immediate[5], Immediate[6], Immediate[7]}), .in1(rt[3:0]), .out(multiplexer_5_out),
    .sel(subOP));
  Multiplexer #(.select(2), .width(2), .enable("false")) multiplexer_6 (
    .in0(2'b00), .in1(2'b01), .in2(2'b10), .out(multiplexer_6_out), .sel(and_2_out));  // open: in3
  Shifter #(.width(16), .shift("lr")) shifter_1 (.in(rs), .\dist (multiplexer_5_out), .out(shifter_1_out));
  Shifter #(.width(16)) shifter_2 (.in(rs), .\dist (multiplexer_5_out), .out(shifter_2_out));
  Multiplexer #(.width(16), .enable("false")) multiplexer_7 (
    .in0(shifter_2_out), .in1(shifter_1_out), .out(multiplexer_7_out), .sel(OPCODE[0]));
  RAM #(.dataWidth(16), .bus("separate")) ram_1 (
    .addr(rt[7:0]), .din(rs), .data(ram_1_data), .str(multiplexer_6_out[0]), .clk(CLOCK),
    .ld(multiplexer_6_out[1]));  // open: sel, clr
  Multiplexer #(.select(2), .width(16), .enable("false")) multiplexer_8 (
    .in0(alu_1_result), .in1(multiplexer_7_out), .in2(ram_1_data), .in3(bit_extender_1_out),
    .out(multiplexer_8_out), .sel(or_2_out));
  not not_18 (not_18_out, OPCODE[1]);
  not not_19 (not_19_out, OPCODE[0]);
  not not_20 (not_20_out, OPCODE[3]);
  and and_4 (and_4_out, not_19_out, not_18_out, not_20_out);
  registerFile Register_File (
    .writeEnable(Write_out), .writeRegister(RS_t), .writeData(multiplexer_8_out), .Clock(CLOCK),
    .readRegister1(RS_t), .readData1(rs), .readRegister2({Immediate[0], Immediate[1], Immediate[2]}),
    .readData2(rt));
  or or_1 (or_2_out[1], and_5_out, and_8_out);
  and and_5 (and_5_out, OPCODE[1], OPCODE[2]);
  not not_21 (not_21_out, OPCODE[1]);
  not not_22 (not_22_out, OPCODE[0]);
  not not_23 (not_23_out, OPCODE[2]);
  not not_24 (not_24_out, OPCODE[0]);
  and and_6 (and_6_out, not_22_out, not_23_out);
  and and_7 (and_7_out, OPCODE[1], not_30_out);
  and and_8 (and_8_out, OPCODE[0], not_21_out, not_25_out, OPCODE[3], subOP);
  not not_25 (not_25_out, OPCODE[2]);
  not not_26 (not_26_out, OPCODE[3]);
  not not_27 (not_27_out, subOP);
  not not_28 (not_28_out, OPCODE[1]);
  and and_9 (and_9_out, not_24_out, not_26_out, not_27_out);
  or Write (Write_out, and_4_out, and_6_out, and_9_out, and_11_out, and_12_out);
  or or_2 (or_2_out[0], and_7_out, and_10_out, and_13_out);
  and and_10 (and_10_out, OPCODE[0], not_29_out, OPCODE[3], subOP);
  not not_29 (not_29_out, OPCODE[2]);
  not not_30 (not_30_out, OPCODE[2]);
  not not_31 (not_31_out, OPCODE[1]);
  and and_11 (and_11_out, OPCODE[0], not_28_out, OPCODE[3], subOP);
  and and_12 (and_12_out, OPCODE[0], not_31_out, OPCODE[2], not_32_out);
  and and_13 (and_13_out, OPCODE[0], OPCODE[1]);
  not not_32 (not_32_out, subOP);
  ALU alu_1 (.A(rs), .B(multiplexer_9_out), .Operation({OPCODE[0], or_3_out[0]}), .Result(alu_1_result));
  Multiplexer #(.width(16), .enable("false")) multiplexer_9 (
    .in0(rt), .in1(multiplexer_10_out), .out(multiplexer_9_out), .sel(Format));
  assign bit_extender_2_out = {{8{Immediate[7]}}, Immediate};  // Bit_Extender bit_extender_2
  not not_33 (not_33_out, OPCODE[2]);
  Multiplexer #(.width(16), .enable("false")) multiplexer_10 (
    .in0(bit_extender_3_out), .in1(bit_extender_2_out), .out(multiplexer_10_out), .sel(subOP));
  or or_3 (or_3_out[0], not_33_out, OPCODE[3]);
  assign bit_extender_3_out = {{8{1'b0}}, Immediate};  // Bit_Extender bit_extender_3

  // Other names for the same wires on the sheet: shiftAmount[3:0] = {Immediate[4], Immediate[5], Immediate[6], Immediate[7]};
  //   RT_t[2:0] = {Immediate[0], Immediate[1], Immediate[2]}

  // Notes on the sheet:
  //   Halt Execution
  //   InstructionMemory
  //   PC
  //   Put Execution
  //   Sabrina Aravena
  //   SAA154@pitt.edu
  //   JrMIPS
  //   PC + 1
  //   Data Memory
  //   Shift
  //   ALU
endmodule

module registerFile (
  input  writeEnable,
  input  [2:0] readRegister1,
  input  [2:0] readRegister2,
  input  [2:0] writeRegister,
  input  [15:0] writeData,
  input  Clock,
  output [15:0] readData1,
  output [15:0] readData2
);

  wire demultiplexer_1_out0, demultiplexer_1_out1, demultiplexer_1_out2, demultiplexer_1_out3,
       demultiplexer_1_out4, demultiplexer_1_out5, demultiplexer_1_out6, demultiplexer_1_out7;
  wire [15:0] demultiplexer_2_out0, demultiplexer_2_out1, demultiplexer_2_out2, demultiplexer_2_out3,
       demultiplexer_2_out4, demultiplexer_2_out5, demultiplexer_2_out6, demultiplexer_2_out7, register_1_q,
       register_2_q, register_3_q, register_4_q, register_5_q, register_6_q, register_7_q, register_8_q;

  Demultiplexer #(.select(3), .enable("false")) demultiplexer_1 (
    .out0(demultiplexer_1_out0), .out1(demultiplexer_1_out1), .out2(demultiplexer_1_out2),
    .out3(demultiplexer_1_out3), .out4(demultiplexer_1_out4), .out5(demultiplexer_1_out5),
    .out6(demultiplexer_1_out6), .out7(demultiplexer_1_out7), .in(writeEnable), .sel(writeRegister));
  Demultiplexer #(.select(3), .width(16), .enable("false")) demultiplexer_2 (
    .out0(demultiplexer_2_out0), .out1(demultiplexer_2_out1), .out2(demultiplexer_2_out2),
    .out3(demultiplexer_2_out3), .out4(demultiplexer_2_out4), .out5(demultiplexer_2_out5),
    .out6(demultiplexer_2_out6), .out7(demultiplexer_2_out7), .in(writeData), .sel(writeRegister));
  Register #(.width(16)) register_1 (
    .D(demultiplexer_2_out0), .en(demultiplexer_1_out0), .Q(register_1_q), .clk(Clock));  // open: clr
  Register #(.width(16)) register_2 (
    .D(demultiplexer_2_out1), .en(demultiplexer_1_out1), .Q(register_2_q), .clk(Clock));  // open: clr
  Register #(.width(16)) register_3 (
    .D(demultiplexer_2_out2), .en(demultiplexer_1_out2), .Q(register_3_q), .clk(Clock));  // open: clr
  Register #(.width(16)) register_4 (
    .D(demultiplexer_2_out3), .en(demultiplexer_1_out3), .Q(register_4_q), .clk(Clock));  // open: clr
  Register #(.width(16)) register_5 (
    .D(demultiplexer_2_out4), .en(demultiplexer_1_out4), .Q(register_5_q), .clk(Clock));  // open: clr
  Register #(.width(16)) register_6 (
    .D(demultiplexer_2_out5), .en(demultiplexer_1_out5), .Q(register_6_q), .clk(Clock));  // open: clr
  Register #(.width(16)) register_7 (
    .D(demultiplexer_2_out6), .en(demultiplexer_1_out6), .Q(register_7_q), .clk(Clock));  // open: clr
  Register #(.width(16)) register_8 (
    .D(demultiplexer_2_out7), .en(demultiplexer_1_out7), .Q(register_8_q), .clk(Clock));  // open: clr
  Multiplexer #(.select(3), .width(16), .enable("false")) multiplexer_1 (
    .in0(register_1_q), .in1(register_2_q), .in2(register_3_q), .in3(register_4_q), .in4(register_5_q),
    .in5(register_6_q), .in6(register_7_q), .in7(register_8_q), .out(readData1), .sel(readRegister1));
  Multiplexer #(.select(3), .width(16), .enable("false")) multiplexer_2 (
    .in0(register_1_q), .in1(register_2_q), .in2(register_3_q), .in3(register_4_q), .in4(register_5_q),
    .in5(register_6_q), .in6(register_7_q), .in7(register_8_q), .out(readData2), .sel(readRegister2));
endmodule

module ALU (
  input  [15:0] A,
  input  [15:0] B,
  input  [1:0] Operation,
  output [15:0] Result
);

  wire [15:0] adder_1_out, and_1_out, nor_1_out, subtractor_1_out;

  Adder #(.width(16)) adder_1 (.a(A), .b(B), .out(adder_1_out));  // open: cin, cout
  Subtractor #(.width(16)) subtractor_1 (.a(A), .b(B), .out(subtractor_1_out));  // open: bin, bout
  assign and_1_out = A & B;  // AND_Gate and_1, 16 bits wide
  assign nor_1_out = ~(A | B);  // NOR_Gate nor_1, 16 bits wide
  Multiplexer #(.select(2), .width(16), .enable("false")) multiplexer_1 (
    .in0(and_1_out), .in1(nor_1_out), .in2(adder_1_out), .in3(subtractor_1_out), .out(Result), .sel(Operation));
endmodule

module Decoder (
  input  [4:0] Operation,
  output Select
);

  wire and_1_out, and_2_out, and_3_out, and_4_out, not_1_out, not_2_out, not_3_out, not_4_out, not_5_out,
       not_6_out, not_7_out;

  not not_1 (not_1_out, Operation[1]);
  not not_2 (not_2_out, Operation[2]);
  not not_3 (not_3_out, Operation[3]);
  not not_4 (not_4_out, Operation[0]);
  not not_5 (not_5_out, Operation[1]);
  not not_6 (not_6_out, Operation[2]);
  not not_7 (not_7_out, Operation[2]);
  and and_1 (and_1_out, not_1_out, not_2_out, not_3_out);
  and and_2 (and_2_out, not_4_out, Operation[2], Operation[3]);
  and and_3 (and_3_out, Operation[0], not_5_out, not_6_out, Operation[4]);
  and and_4 (and_4_out, Operation[0], Operation[1], not_7_out, Operation[3]);
  or or_1 (Select, and_1_out, and_2_out, and_3_out, and_4_out);
endmodule

module Branch (
  input  [3:0] Operation,
  input  subOP,
  input  [15:0] rs,
  output Output
);

  wire and_1_out, and_2_out, and_3_out, and_4_out, and_5_out, and_6_out, and_7_out, and_8_out, and_9_out,
       comparator_1_eq, comparator_1_gt, comparator_1_lt, not_1_out, not_2_out, not_3_out, not_4_out,
       not_5_out, not_6_out, not_7_out, not_8_out, not_9_out, not_10_out, not_11_out, not_12_out, not_13_out,
       not_14_out, not_15_out, not_16_out, not_17_out, not_18_out, not_19_out, not_20_out, not_21_out,
       not_22_out, not_23_out, or_1_out, or_2_out;

  not not_1 (not_1_out, Operation[0]);
  not not_2 (not_2_out, Operation[1]);
  not not_3 (not_3_out, Operation[2]);
  not not_4 (not_4_out, Operation[3]);
  not not_5 (not_5_out, Operation[1]);
  not not_6 (not_6_out, Operation[2]);
  not not_7 (not_7_out, Operation[3]);
  not not_8 (not_8_out, Operation[0]);
  not not_9 (not_9_out, Operation[1]);
  not not_10 (not_10_out, Operation[2]);
  not not_11 (not_11_out, Operation[3]);
  and and_1 (and_1_out, not_1_out, Operation[1], Operation[2], Operation[3]);
  and and_2 (and_2_out, Operation[0], not_2_out, not_3_out, not_4_out);
  and and_3 (and_3_out, Operation[0], not_5_out, not_6_out, not_7_out);
  and and_4 (and_4_out, not_8_out, Operation[1], Operation[2], Operation[3], subOP);
  and and_5 (and_5_out, Operation[0], not_9_out, not_10_out, not_11_out, subOP);
  or or_1 (or_1_out, and_1_out, and_2_out);
  or or_2 (or_2_out, and_4_out, and_5_out);
  Comparator #(.width(16)) comparator_1 (
    .a(rs), .b({16{1'b0}}), .gt(comparator_1_gt), .eq(comparator_1_eq), .lt(comparator_1_lt));
  not not_12 (not_12_out, or_2_out);
  not not_13 (not_13_out, comparator_1_gt);
  not not_14 (not_14_out, comparator_1_eq);
  not not_15 (not_15_out, and_3_out);
  not not_16 (not_16_out, or_2_out);
  not not_17 (not_17_out, comparator_1_eq);
  not not_18 (not_18_out, comparator_1_lt);
  not not_19 (not_19_out, and_3_out);
  not not_20 (not_20_out, comparator_1_gt);
  not not_21 (not_21_out, comparator_1_lt);
  not not_22 (not_22_out, comparator_1_eq);
  not not_23 (not_23_out, comparator_1_lt);
  and and_6 (and_6_out, or_1_out, not_12_out, not_13_out, not_14_out, comparator_1_lt);
  and and_7 (and_7_out, or_1_out, not_15_out, not_16_out, comparator_1_gt, not_17_out, not_18_out);
  and and_8 (and_8_out, or_1_out, not_19_out, or_2_out, not_20_out, comparator_1_eq, not_21_out);
  and and_9 (and_9_out, or_1_out, and_3_out, or_2_out, comparator_1_gt, not_22_out, not_23_out);
  or or_3 (Output, and_6_out, and_7_out, and_8_out, and_9_out);
endmodule
